# Fritzing sketch hello_world_v1 (saved by Fritzing 0.9.9b)
breadboards: 1

parts:
  R1 = Resistor [tolerance=±5% power=0.25 resistance=220 package=THT]
  LED1 = LED - 5mm [color="Red (633nm)" current=0.030 package="5 mm [THT]"]
  Componente1 = Arduino Nano 33 BLE Sense

nets:
  N1: R1.Pin_0, LED1.anode
  N2: R1.Pin_1, Componente1.D2
  N3: LED1.cathode, Componente1.GND, Componente1.A7
  N4: Componente1.D11/MOSI, Componente1.+5V

custom parts:
  Arduino Nano 33 BLE Sense: The Nano 33 BLE Sense (without headers) is Arduino’s 3.3V AI enabled board in the smallest available form factor: 45x18mm! The Arduino Nano 33 BLE Sense is a completely new board on a well-known form factor. It comes with a series of embedded sensors: 9 axis inertial sensor: what makes this board ideal for wearable devices humidity, and temperature sensor: to get highly accurate measurements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
